// Logisim project 6190_NAND.circ as structural Verilog: 1 circuit, main circuit main
module main (
  input  x1,
  input  x2,
  input  x3,
  input  x4,
  output out_5
);

  wire nand_1_out, nand_2_out, nand_3_out, nand_4_out, nand_5_out, nand_6_out, nand_7_out;

  nand nand_1 (nand_1_out, x2, x2);
  nand nand_2 (nand_2_out, x1, x1);
  nand nand_3 (nand_3_out, x4, x4);
  nand nand_4 (nand_4_out, nand_2_out, x2, x3, nand_3_out);
  nand nand_5 (nand_5_out, x3, x3);
  nand nand_6 (nand_6_out, nand_2_out, nand_1_out, nand_5_out);
  nand nand_7 (nand_7_out, nand_2_out, nand_5_out, x4);
  nand nand_8 (out_5, nand_4_out, nand_6_out, nand_7_out);
endmodule
