// Logisim project 6190_NOR.circ as structural Verilog: 1 circuit, main circuit main
module main (
  input  x1,
  input  x2,
  input  x3,
  input  x4,
  output out_5
);

  wire nand_1_out, nand_2_out, nand_3_out, not_1_out, not_2_out, not_3_out, not_4_out;

  not not_1 (not_1_out, x1);
  not not_2 (not_2_out, x2);
  not not_3 (not_3_out, x3);
  not not_4 (not_4_out, x4);
  nand nand_1 (nand_1_out, not_1_out, not_2_out, not_3_out);
  nand nand_2 (nand_2_out, not_1_out, x2, not_4_out, x3);
  nand nand_3 (nand_3_out, x1, not_2_out, not_3_out, x4);
  nand nand_4 (out_5, nand_3_out, nand_1_out, nand_2_out);
endmodule
