// Logisim project cwiczenia6.circ as structural Verilog: 3 circuits, main circuit cw 2_3
module cw_2_3 (
  input  in_1,
  input  [3:0] in_2,
  input  [3:0] in_3,
  input  [3:0] in_4,
  output out_5
);

  Adder #(.width(4)) adder_1 (.a(in_3), .b(in_4), .out(in_2), .cin(in_1), .cout(out_5));
endmodule

module cw4 (
  input  [3:0] in_1,
  input  [3:0] in_2,
  input  [3:0] in_3,
  output out_4,
  output out_5
);

  wire adder_1_cout, adder_2_cout, adder_3_cout;

  Adder #(.width(1)) adder_1 (.a(in_1[0]), .b(in_2[0]), .out(in_3[0]), .cin(1'b0), .cout(adder_1_cout));
  Adder #(.width(1)) adder_2 (.a(in_1[1]), .b(in_2[1]), .out(in_3[1]), .cin(adder_1_cout), .cout(adder_2_cout));
  Adder #(.width(1)) adder_3 (.a(in_1[2]), .b(in_2[2]), .out(in_3[2]), .cin(adder_2_cout), .cout(adder_3_cout));
  Adder #(.width(1)) adder_4 (.a(in_1[3]), .b(in_2[3]), .out(in_3[3]), .cin(adder_3_cout), .cout(out_5));
  xor xor_1 (out_4, out_5, adder_3_cout);
endmodule

module cwi_1 (
  input  x1,
  input  x0,
  input  Cin,
  output y,
  output Cout
);

  wire nand_1_out, nand_2_out, nand_3_out, nand_4_out, nand_5_out, nand_6_out, nand_7_out, nand_8_out,
       nand_9_out, nand_10_out, nand_11_out, nand_12_out, nand_13_out;

  nand nand_1 (nand_1_out, x1, x1);
  nand nand_2 (nand_2_out, x0, x0);
  nand nand_3 (nand_3_out, x1, x1);
  nand nand_4 (nand_4_out, Cin, Cin);
  nand nand_5 (nand_5_out, x0, x0);
  nand nand_6 (nand_6_out, Cin, Cin);
  nand nand_7 (nand_7_out, x1, Cin);
  nand nand_8 (nand_8_out, x1, x0);
  nand nand_9 (nand_9_out, x0, Cin);
  nand nand_10 (nand_10_out, nand_1_out, nand_2_out, Cin);
  nand nand_11 (nand_11_out, nand_3_out, x0, nand_4_out);
  nand nand_12 (nand_12_out, x1, nand_5_out, nand_6_out);
  nand nand_13 (nand_13_out, x1, x0, Cin);
  nand nand_14 (Cout, nand_7_out, nand_8_out, nand_9_out);
  nand nand_15 (y, nand_10_out, nand_11_out, nand_12_out, nand_13_out);
endmodule
