// Logisim project cwiczenia7.circ as structural Verilog: 2 circuits, main circuit cw1_2
module cw1_2 (
  output [7:0] out_1
);

  wire button_1_out, clock_1_out, not_1_out;
  wire [7:0] controlled_buffer_1_out, counter_1_q, rom_1_data;

  Button button_1 (.out(button_1_out));
  Clock clock_1 (.out(clock_1_out));
  Counter counter_1 (
    .load(1'b0), .D({8{1'b0}}), .count(1'b1), .Q(counter_1_q), .clk(clock_1_out), .clr(button_1_out));  // open: carry
  not not_1 (not_1_out, 1'b0);
  assign controlled_buffer_1_out = 1'b0 ? counter_1_q : 8'bz;  // Controlled_Buffer controlled_buffer_1
  RAM ram_1 (.addr(counter_1_q), .data(out_1), .sel(1'b1), .ld(button_1_out), .clr(1'b0));  // open: clk
  ROM rom_1 (.addr(counter_1_q), .data(rom_1_data), .sel(1'b1));
  assign controlled_buffer_1_out = not_1_out ? rom_1_data : 8'bz;  // Controlled_Buffer controlled_buffer_2

  // Notes on the sheet:
  //   contents of rom_1 (hex, n*v repeats v):
  //   0 1 2 3 4 5 6 7 8 9 a b c d e f 10 11 12 13 14 15 16 17 18 19 1a 1b 1c 1d 1e 1f 20 21 22 23 24 25 26
  //   27 28 29 2a 2b 2c 2d 2e 2f 30 31 32 33 34 35 36 37 38 39 3a 3b 3c 3d 3e 3f 40 41 42 43 44 45 46 47
  //   48 49 4a 4b 4c 4d 4e 4f 50 51 52 53 54 55 56 57 58 59 5a 5b 5c 5d 5e 5f 60 61 62 63 64 65 66 67 68
  //   69 6a 6b 6c 6d 6e 6f 70 71 72 73 74 75 76 77 78 79 7a 7b 7c 7d 7e 7f 80 81 82 83 84 85 86 87 88 89
  //   8a 8b 8c 8d 8e 8f 90 91 92 93 94 95 96 97 98 99 9a 9b 9c 9d 9e 9f a0 a1 a2 a3 a4 a5 a6 a7 a8 a9 aa
  //   ab ac ad ae af b0 b1 b2 b3 b4 b5 b6 b7 b8 b9 ba bb bc bd be bf c0 c1 c2 c3 c4 c5 c6 c7 c8 c9 ca cb
  //   cc cd ce cf d0 d1 d2 d3 d4 d5 d6 d7 d8 d9 da db dc dd de df e0 e1 e2 e3 e4 e5 e6 e7 e8 e9 ea eb ec
  //   ed ee ef f0 f1 f2 f3 f4 f5 f6 f7 f8 f9 fa fb fc fd fe ff
endmodule

module cw3 (
  input  [15:0] in_1,
  output [7:0] out_2
);

  wire button_1_out, demultiplexer_1_out0, demultiplexer_1_out1, demultiplexer_1_out2, demultiplexer_1_out3,
       or_1_out;

  Demultiplexer #(.select(2), .enable("false")) demultiplexer_1 (
    .out0(demultiplexer_1_out0), .out1(demultiplexer_1_out1), .out2(demultiplexer_1_out2),
    .out3(demultiplexer_1_out3), .in(1'b1), .sel(in_1[15:14]));
  or or_1 (or_1_out, demultiplexer_1_out2, demultiplexer_1_out3);
  ROM #(.addrWidth(14)) rom_1 (.addr(in_1[13:0]), .data(out_2), .sel(demultiplexer_1_out0));
  RAM #(.addrWidth(14)) ram_1 (
    .addr(in_1[13:0]), .data(out_2), .sel(demultiplexer_1_out1), .ld(1'b1), .clr(button_1_out));  // open: clk
  RAM #(.addrWidth(15)) ram_2 (
    .addr(in_1[14:0]), .data(out_2), .sel(or_1_out), .ld(1'b1), .clr(button_1_out));  // open: clk
  Button button_1 (.out(button_1_out));
endmodule
