// Logisim project cwiczenia7_proba.circ as structural Verilog: 2 circuits, main circuit zadanie 1 i 2
module zadanie_1_i_2 (
  input  in_1,
  input  in_2,
  output [7:0] out_3
);

  wire clock_1_out;
  wire [7:0] counter_1_q;

  Clock clock_1 (.out(clock_1_out));
  Counter counter_1 (.Q(counter_1_q), .clk(clock_1_out));  // open: load, D, count, carry, clr
  RAM ram_1 (.addr(counter_1_q), .data(out_3), .sel(in_1), .clk(clock_1_out), .ld(in_2));  // open: clr
  ROM rom_1 (.addr(counter_1_q), .data(out_3), .sel(in_1));

  // Notes on the sheet:
  //   contents of rom_1 (hex, n*v repeats v):
  //   ff ff 0 11*ff e f 10 11 12 13 14 15 16 17 18 19 1a 1b 1c 1d 1e 1f 20 21 22 23
endmodule

module zadanie_3 (
  input  [15:0] in_1,
  output [7:0] out_2
);

  wire button_1_out, demultiplexer_1_out0, demultiplexer_1_out1, demultiplexer_1_out2, demultiplexer_1_out3,
       or_1_out;

  Demultiplexer #(.select(2), .enable("false")) demultiplexer_1 (
    .out0(demultiplexer_1_out0), .out1(demultiplexer_1_out1), .out2(demultiplexer_1_out2),
    .out3(demultiplexer_1_out3), .in(1'b1), .sel(in_1[15:14]));
  or or_1 (or_1_out, demultiplexer_1_out1, demultiplexer_1_out2);
  ROM #(.addrWidth(14)) rom_1 (.addr(in_1[13:0]), .data(out_2), .sel(demultiplexer_1_out0));
  RAM #(.addrWidth(14), .bus("asynch")) ram_1 (
    .addr(in_1[13:0]), .data(out_2), .sel(or_1_out), .ld(1'b1), .clr(button_1_out));
  RAM #(.addrWidth(15), .bus("asynch")) ram_2 (
    .addr(in_1[14:0]), .data(out_2), .sel(demultiplexer_1_out3), .ld(1'b1), .clr(button_1_out));
  Button button_1 (.out(button_1_out));

  // Notes on the sheet:
  //   contents of rom_1 (hex, n*v repeats v):
  //   ff ff 0 11*ff e f 10 11 12 13 14 15 16 17 18 19 1a 1b 1c 1d 1e 1f 20 21 22 23
endmodule
