// Logisim project zajecia1_przyklady.circ as structural Verilog: 3 circuits, main circuit main
module main (
  input  in_1,
  input  in_2,
  input  in_3,
  input  in_4,
  input  a_b,
  input  in_6,
  input  in_7,
  input  in_8,
  input  in_9,
  output out_10,
  output out_11,
  output out_12,
  output out_13
);

  wire not_1_out, or_1_out;

  not not_1 (not_1_out, in_7);
  Transistor transistor_1 (.in(in_4), .out(out_11), .gate(in_3));
  or or_1 (or_1_out, a_b, in_6);
  Pull_Resistor pull_resistor_1 (.node(out_11));
  and and_1 (out_12, or_1_out, not_1_out);
  and and_2 (out_10, in_1, in_2);
  Bramka_AND bramka_and_1 (.in_1(in_8), .in_2(in_9), .out_3(out_13));

  // Notes on the sheet:
  //   neg.C
  //   y=(a+b)*neg. C
  //   Wlasna bramka AND wbudowana w blackbox
endmodule

module Bramka_AND (
  input  in_1,
  input  in_2,
  output out_3
);

  and and_1 (out_3, in_1, in_2);
endmodule

module wygenerowany (
  input  a,
  input  b,
  input  c,
  output y
);

  wire and_1_out, and_2_out, not_1_out, not_2_out;

  not not_1 (not_1_out, a);
  not not_2 (not_2_out, b);
  and and_1 (and_1_out, not_1_out, b);
  and and_2 (and_2_out, a, not_2_out, c);
  or or_1 (y, and_1_out, and_2_out);
endmodule
