// Logisim project zajecia2_dokonczyć.circ as structural Verilog: 1 circuit, main circuit main
module main (
  input  a,
  input  b,
  input  c,
  input  d,
  input  a_2,
  input  b_2,
  input  c_2,
  input  d_2,
  output out_9
);

  wire nand_1_out, nand_2_out, nand_3_out, nand_4_out, nand_9_out, nand_10_out, nand_11_out;

  nand nand_1 (nand_1_out, a, a);
  nand nand_2 (nand_2_out, b, b);
  nand nand_3 (nand_3_out, c, c);
  nand nand_4 (nand_4_out, d, d);
  // NAND_Gate nand_5 has open pins: in0=a_2, in3=a_2, out=open
  // NAND_Gate nand_6 has open pins: in0=b_2, in3=b_2, out=open
  // NAND_Gate nand_7 has open pins: in0=c_2, in4=c_2, out=open
  // NAND_Gate nand_8 has open pins: in0=d_2, in3=d_2, out=open
  nand nand_9 (nand_9_out, nand_1_out, b, nand_4_out);
  nand nand_10 (nand_10_out, nand_4_out, nand_3_out);
  nand nand_11 (nand_11_out, nand_2_out, nand_3_out);
  nand nand_12 (out_9, nand_9_out, nand_10_out, nand_11_out);

  // Notes on the sheet:
  //   y=E{0,1,4,6,8,9}         y=NIEabNIEd+NIEcNIEd+NIEbNIEc
  //   y=E(5,7,11,12,15}    y=abNIEcNIEd+NIEabd+acd
endmodule
