// Logisim project zajecia2_robota.circ as structural Verilog: 1 circuit, main circuit R
module R (
  input  L,
  input  F,
  input  R,
  output out_4,
  output out_5
);

  wire nor_1_out, nor_2_out, nor_3_out, nor_4_out, nor_5_out, nor_6_out;

  nor nor_1 (nor_1_out, L, L);
  nor nor_2 (nor_2_out, F, F);
  nor nor_3 (nor_3_out, R, R);
  nor nor_4 (nor_4_out, nor_3_out, nor_2_out);
  nor nor_5 (nor_5_out, nor_1_out, nor_2_out);
  nor nor_6 (nor_6_out, nor_2_out, R);
  not not_1 (out_4, nor_4_out);
  nor nor_7 (out_5, nor_5_out, nor_6_out);

  // Notes on the sheet:
  //   ROBOT
  //   nieF+nieR
  //   (nieL+nieF)*(nieF+R)
  //   nieL
endmodule
