// Logisim project zajecia3_MUX.circ as structural Verilog: 1 circuit, main circuit main
module main (
  input  X3,
  input  [2:0] in_2,
  input  [3:0] in_3,
  input  in_4,
  input  in_5,
  input  [1:0] in_6,
  output out_7,
  output out_8,
  output out_9
);

  wire and_1_out, and_2_out, not_1_out, not_2_out, or_1_out;

  Multiplexer #(.select(4)) multiplexer_1 (
    .in0(1'b0), .in1(1'b0), .in2(1'b0), .in3(1'b0), .in4(1'b0), .in5(1'b1), .in6(1'b0), .in7(1'b1),
    .in8(1'b0), .in9(1'b0), .in10(1'b0), .in11(1'b1), .in12(1'b1), .in13(1'b0), .in14(1'b0), .in15(1'b1),
    .out(out_8), .sel(in_3));  // open: en
  not not_1 (not_1_out, in_4);
  and and_1 (and_1_out, in_4, in_5);
  and and_2 (and_2_out, not_1_out, in_5);
  not not_2 (not_2_out, X3);
  or or_1 (or_1_out, in_4, in_5);
  Multiplexer #(.select(3)) multiplexer_2 (
    .in0(1'b0), .in1(1'b0), .in2(1'b0), .in3(X3), .in4(X3), .in5(not_2_out), .in6(1'b0), .in7(1'b1),
    .out(out_7), .sel(in_2));  // open: en
  Multiplexer #(.select(2)) multiplexer_3 (
    .in0(and_1_out), .in1(and_2_out), .in2(1'b0), .in3(or_1_out), .out(out_9), .sel(in_6));  // open: en

  // Notes on the sheet:
  //   x0
  //   x1
  //   y= 5,7,11,12,15
endmodule
