// Logisim project zajecia4_przerzutniki.circ as structural Verilog: 5 circuits, main circuit main
module main (
  input  in_1,
  input  S,
  input  C,
  input  in_4,
  input  in_5,
  input  preset,
  input  D,
  input  in_8,
  input  in_9,
  input  in_10,
  input  in_11,
  output out_12,
  output out_13,
  output out_14,
  output out_15,
  output out_16,
  output out_17,
  output licznik_mod9,
  output out_19,
  output out_20,
  output out_21,
  output out_22,
  output out_23,
  output out_24,
  output out_25,
  output out_26,
  output out_27,
  output out_28,
  output out_29,
  output out_30,
  output out_31,
  output out_32,
  output out_33
);

  wire and_1_out, and_2_out, clock_1_out, clock_2_out, clock_3_out, clock_4_out, clock_5_out, clock_6_out,
       clock_7_out, clock_8_out, clock_9_out, d_ff_1_q, d_ff_2_q, d_ff_3_q, d_ff_4_qn, d_ff_5_qn, d_ff_6_q,
       d_ff_7_q, d_ff_8_q, d_ff_9_qn, d_ff_10_qn, d_ff_11_q, d_ff_12_q, d_ff_13_q, d_ff_14_qn, d_ff_15_qn,
       d_ff_17_q, d_ff_18_qn, d_ff_19_qn, d_ff_20_qn, nand_1_out, nand_2_out, not_1_out, undriven,
       undriven_2, undriven_3, xor_1_out;

  Clock clock_1 (.out(clock_1_out));
  Clock clock_2 (.out(clock_2_out));
  Clock clock_3 (.out(clock_3_out));
  Clock clock_4 (.out(clock_4_out));
  Clock clock_5 (.out(clock_5_out));
  D_Flip_Flop d_ff_1 (.clk(clock_1_out), .D(in_1), .Q(d_ff_1_q), .reset(undriven));  // open: Qn, preset, en
  D_Flip_Flop d_ff_2 (.clk(clock_2_out), .D(d_ff_17_q), .Q(d_ff_2_q), .preset(in_4));  // open: Qn, en, reset
  D_Flip_Flop d_ff_3 (.clk(clock_3_out), .D(d_ff_18_qn), .Q(d_ff_3_q), .reset(undriven_2));  // open: Qn, preset, en
  D_Flip_Flop d_ff_4 (
    .clk(clock_4_out), .D(d_ff_4_qn), .Q(out_21), .Qn(d_ff_4_qn), .reset(and_1_out));  // open: preset, en
  D_Flip_Flop d_ff_5 (
    .clk(clock_5_out), .D(d_ff_5_qn), .Q(out_29), .Qn(d_ff_5_qn), .preset(and_2_out));  // open: en, reset
  D_Flip_Flop d_ff_6 (.clk(clock_1_out), .D(d_ff_1_q), .Q(d_ff_6_q), .reset(undriven));  // open: Qn, preset, en
  D_Flip_Flop d_ff_7 (.clk(clock_2_out), .D(d_ff_2_q), .Q(d_ff_7_q), .reset(in_4));  // open: Qn, preset, en
  D_Flip_Flop d_ff_8 (.clk(clock_3_out), .D(d_ff_3_q), .Q(d_ff_8_q), .reset(undriven_2));  // open: Qn, preset, en
  D_Flip_Flop d_ff_9 (
    .clk(d_ff_4_qn), .D(d_ff_9_qn), .Q(out_20), .Qn(d_ff_9_qn), .reset(and_1_out));  // open: preset, en
  D_Flip_Flop d_ff_10 (
    .clk(d_ff_5_qn), .D(d_ff_10_qn), .Q(out_28), .Qn(d_ff_10_qn), .preset(and_2_out));  // open: en, reset
  D_Flip_Flop d_ff_11 (.clk(clock_1_out), .D(d_ff_6_q), .Q(d_ff_11_q), .reset(undriven));  // open: Qn, preset, en
  D_Flip_Flop d_ff_12 (.clk(clock_2_out), .D(d_ff_7_q), .Q(d_ff_12_q), .reset(in_4));  // open: Qn, preset, en
  D_Flip_Flop d_ff_13 (.clk(clock_3_out), .D(d_ff_8_q), .Q(d_ff_13_q), .reset(undriven_2));  // open: Qn, preset, en
  D_Flip_Flop d_ff_14 (
    .clk(d_ff_9_qn), .D(d_ff_14_qn), .Q(out_19), .Qn(d_ff_14_qn), .reset(and_1_out));  // open: preset, en
  D_Flip_Flop d_ff_15 (
    .clk(d_ff_10_qn), .D(d_ff_15_qn), .Q(out_27), .Qn(d_ff_15_qn), .reset(and_2_out));  // open: preset, en
  Clock clock_6 (.out(clock_6_out));
  D_Flip_Flop d_ff_16 (.clk(clock_1_out), .D(d_ff_11_q), .reset(undriven));  // open: Q, Qn, preset, en
  D_Flip_Flop d_ff_17 (.clk(clock_2_out), .D(d_ff_12_q), .Q(d_ff_17_q), .reset(in_4));  // open: Qn, preset, en
  D_Flip_Flop d_ff_18 (.clk(clock_3_out), .D(d_ff_13_q), .Qn(d_ff_18_qn), .reset(undriven_2));  // open: Q, preset, en
  D_Flip_Flop d_ff_19 (
    .clk(d_ff_14_qn), .D(d_ff_19_qn), .Q(licznik_mod9), .Qn(d_ff_19_qn), .reset(and_1_out));  // open: preset, en
  Johnson johnson_1 (.clock(clock_6_out), .Q1(in_8), .Q2(in_9), .Q3(in_10), .Q4(in_11));
  and and_1 (and_1_out, out_21, licznik_mod9);
  D_Flip_Flop d_ff_20 (
    .clk(d_ff_15_qn), .D(d_ff_20_qn), .Q(out_26), .Qn(d_ff_20_qn), .reset(and_2_out));  // open: preset, en
  not not_1 (not_1_out, S);
  Clock clock_7 (.out(clock_7_out));
  and and_2 (and_2_out, out_26, out_28);
  D_Flip_Flop d_ff_21 (.clk(clock_7_out), .D(xor_1_out), .Q(out_17));  // open: Qn, preset, en, reset
  D_Flip_Flop d_ff_22 (.clk(clock_7_out), .D(out_17), .Q(out_16));  // open: Qn, preset, en, reset
  Clock clock_8 (.out(clock_8_out));
  Clock clock_9 (.out(clock_9_out));
  nand nand_1 (nand_1_out, S, C);
  nand nand_2 (nand_2_out, C, not_1_out);
  _4bit_rejestr_przesuwny u_4bit_rejestr_przesuwny_1 (
    .D(in_5), .C(clock_8_out), .out_3(out_22), .out_4(out_23), .out_5(out_24), .out_6(out_25));
  D d_1 (.PRESET(preset), .CLEAR(undriven_3), .CLOCK(clock_9_out), .D(D), .Q(out_30));  // open: notQ
  nand nand_3 (out_12, nand_1_out, out_13);
  nand nand_4 (out_13, out_12, nand_2_out);
  D_Flip_Flop d_ff_23 (.clk(clock_7_out), .D(out_16), .Q(out_15));  // open: Qn, preset, en, reset
  D d_2 (.PRESET(preset), .CLEAR(undriven_3), .CLOCK(clock_9_out), .D(out_30), .Q(out_31));  // open: notQ
  D d_3 (.PRESET(preset), .CLEAR(undriven_3), .CLOCK(clock_9_out), .D(out_31), .Q(out_32));  // open: notQ
  D_Flip_Flop d_ff_24 (.clk(clock_7_out), .D(out_15), .Q(out_14));  // open: Qn, preset, en, reset
  xor xor_1 (xor_1_out, out_14, out_15);
  D d_4 (.PRESET(preset), .CLEAR(undriven_3), .CLOCK(clock_9_out), .D(out_32), .Q(out_33));  // open: notQ

  // Notes on the sheet:
  //   Czterobitowy rejestr przesuwny.
  //   Licznik pierscieniowy
  //   Licznik Johnsona
  //   wpierw idzie cały cykl a następnie od 3-9 w pętli
  //   licznik od 3 do 9
  //   R
  //   Zatrzask 1 bitowy
  //   sekwencja stanów pseudolosowych
  //   Czterobitowy rejestr przesuwny oparty na przerzutnikach D typu Latch
  //   Czterobitowy rejestr przesuwny.
endmodule

module _4bit_rejestr_przesuwny (
  input  D,
  input  C,
  output out_3,
  output out_4,
  output out_5,
  output out_6
);

  wire nand_1_out, nand_2_out, nand_4_out, nand_5_out, nand_6_out, nand_8_out, nand_9_out, nand_10_out,
       nand_12_out, nand_13_out, nand_14_out, nand_16_out;

  nand nand_1 (nand_1_out, D, C);
  nand nand_2 (nand_2_out, nand_1_out, C);
  nand nand_3 (out_3, nand_1_out, nand_4_out);
  nand nand_4 (nand_4_out, out_3, nand_2_out);
  nand nand_5 (nand_5_out, out_3, C);
  nand nand_6 (nand_6_out, nand_5_out, C);
  nand nand_7 (out_4, nand_5_out, nand_8_out);
  nand nand_8 (nand_8_out, out_4, nand_6_out);
  nand nand_9 (nand_9_out, out_4, C);
  nand nand_10 (nand_10_out, nand_9_out, C);
  nand nand_11 (out_5, nand_9_out, nand_12_out);
  nand nand_12 (nand_12_out, out_5, nand_10_out);
  nand nand_13 (nand_13_out, out_5, C);
  nand nand_14 (nand_14_out, nand_13_out, C);
  nand nand_15 (out_6, nand_13_out, nand_16_out);
  nand nand_16 (nand_16_out, out_6, nand_14_out);

  // Notes on the sheet:
  //   4 przerzutniki D typu Latch
endmodule

module przerz_D_wyzwalany_zboczem (
  input  D,
  input  C,
  output Q,
  output nieQ
);

  wire _1_out, _2_out, _3_out, _4_out;

  nand _4 (_4_out, _1_out, _3_out);
  nand _3 (_3_out, _4_out, C);
  nand _2 (_2_out, _3_out, C, _1_out);
  nand _1 (_1_out, _2_out, D);
  or or_1 (Q, _3_out, nieQ);
  or or_2 (nieQ, Q, _2_out);
endmodule

module D (
  input  PRESET,
  input  CLEAR,
  input  CLOCK,
  input  D,
  output Q,
  output notQ
);

  wire nand_1_out, nand_2_out, nand_3_out, nand_4_out, not_1_out, not_2_out;

  not not_1 (not_1_out, CLEAR);
  not not_2 (not_2_out, PRESET);
  nand nand_1 (nand_1_out, not_2_out, nand_4_out, nand_2_out);
  nand nand_2 (nand_2_out, nand_1_out, not_1_out, CLOCK);
  nand nand_3 (nand_3_out, nand_2_out, CLOCK, nand_4_out);
  nand nand_4 (nand_4_out, nand_3_out, not_1_out, D);
  nand nand_5 (Q, not_2_out, nand_2_out, notQ);
  nand nand_6 (notQ, Q, not_1_out, nand_3_out);
endmodule

module Johnson (
  input  clock,
  output Q1,
  output Q2,
  output Q3,
  output Q4
);

  wire d_ff_4_qn, undriven;

  D_Flip_Flop d_ff_1 (.clk(clock), .D(d_ff_4_qn), .Q(Q1), .reset(undriven));  // open: Qn, preset, en
  D_Flip_Flop d_ff_2 (.clk(clock), .D(Q1), .Q(Q2), .reset(undriven));  // open: Qn, preset, en
  D_Flip_Flop d_ff_3 (.clk(clock), .D(Q2), .Q(Q3), .reset(undriven));  // open: Qn, preset, en
  D_Flip_Flop d_ff_4 (.clk(clock), .D(Q3), .Q(Q4), .Qn(d_ff_4_qn), .reset(undriven));  // open: preset, en
endmodule
