// Logisim project zajecia6.circ as structural Verilog: 2 circuits, main circuit cw 2_3
module cw_2_3 (
  input  [3:0] in_1,
  input  [3:0] in_2,
  output [3:0] out_3
);

  wire adder_1_cout;

  Adder #(.width(3)) adder_1 (.a(in_1[2:0]), .b(in_2[2:0]), .out(out_3[2:0]), .cout(adder_1_cout));  // open: cin
  Adder #(.width(1)) adder_2 (.a(in_1[3]), .b(in_2[3]), .out(out_3[3]), .cin(adder_1_cout));  // open: cout
endmodule

module cw4 (
  input  [3:0] in_1,
  input  [3:0] in_2,
  output [3:0] out_3,
  output out_4,
  output out_5
);

  wire adder_1_cout, adder_2_cout, xor_1_out;

  Adder #(.width(3)) adder_1 (.a(in_1[2:0]), .b(in_2[2:0]), .out(out_3[2:0]), .cout(adder_1_cout));  // open: cin
  Adder #(.width(1)) adder_2 (.a(in_1[3]), .b(in_2[3]), .out(out_3[3]), .cin(adder_1_cout), .cout(adder_2_cout));
  xor xor_1 (xor_1_out, adder_2_cout, adder_1_cout);
  and negative (out_4, adder_2_cout, xor_1_out);
  and positive (out_5, adder_1_cout, xor_1_out);
endmodule
