// Logisim project sygnalizacja swietlna.circ as structural Verilog: 1 circuit, main circuit main
module main (
  input  X
);

  wire and_1_out, and_2_out, and_3_out, and_4_out, and_5_out, and_6_out, and_7_out, and_8_out, and_9_out,
       and_10_out, button_1_out, clock_1_out, D0_q, D0_qn, D1_q, D1_qn, D2_q, D2_qn, d_ff_1_q, d_ff_2_q,
       d_ff_3_q, d_ff_3_qn, multiplexer_1_out, not_1_out, or_1_out, or_2_out, or_3_out, or_4_out, or_5_out;

  Clock clock_1 (.out(clock_1_out));
  D_Flip_Flop d_ff_1 (
    .clk(clock_1_out), .D(d_ff_3_qn), .Q(d_ff_1_q), .preset(1'b0), .en(1'b1), .reset(1'b0));  // open: Qn
  not not_1 (not_1_out, X);
  and and_1 (and_1_out, not_1_out, D2_qn, D1_qn, D0_qn);
  and and_2 (and_2_out, D1_q, D0_q, X);
  and and_3 (and_3_out, D2_qn, D1_qn, D0_q, X);
  and and_4 (and_4_out, D1_q, D0_qn, X);
  and and_5 (and_5_out, D2_qn, D1_qn, D0_qn);
  and and_6 (and_6_out, D0_qn, X);
  D_Flip_Flop d_ff_2 (
    .clk(clock_1_out), .D(d_ff_1_q), .Q(d_ff_2_q), .preset(1'b0), .en(1'b1), .reset(1'b0));  // open: Qn
  or or_1 (or_1_out, and_1_out, and_2_out);
  or or_2 (or_2_out, and_3_out, and_4_out);
  or or_3 (or_3_out, and_5_out, and_6_out);
  Button button_1 (.out(button_1_out));
  D_Flip_Flop d_ff_3 (
    .clk(clock_1_out), .D(d_ff_2_q), .Q(d_ff_3_q), .Qn(d_ff_3_qn), .preset(1'b0), .en(1'b1), .reset(1'b0));
  D_Flip_Flop D2 (
    .clk(multiplexer_1_out), .D(or_1_out), .Q(D2_q), .Qn(D2_qn), .preset(1'b0), .en(1'b1),
    .reset(button_1_out));
  D_Flip_Flop D1 (
    .clk(multiplexer_1_out), .D(or_2_out), .Q(D1_q), .Qn(D1_qn), .preset(1'b0), .en(1'b1),
    .reset(button_1_out));
  D_Flip_Flop D0 (
    .clk(multiplexer_1_out), .D(or_3_out), .Q(D0_q), .Qn(D0_qn), .preset(1'b0), .en(1'b1),
    .reset(button_1_out));
  Multiplexer #(.enable("false")) multiplexer_1 (.in0(clock_1_out), .in1(d_ff_3_q), .out(multiplexer_1_out), .sel(X));
  and and_7 (and_7_out, D0_qn, D1_q);
  and and_8 (and_8_out, D2_qn, D1_qn, D0_q);
  and and_9 (and_9_out, D0_qn, D1_q);
  LED led_1 (.in(or_4_out));
  or or_4 (or_4_out, and_7_out, and_8_out);
  LED led_2 (.in(or_5_out));
  LED led_3 (.in(and_10_out));
  or or_5 (or_5_out, D2_q, and_9_out);
  and and_10 (and_10_out, D1_q, D0_q);

  // Notes on the sheet:
  //   Sygnalizacja świetlna: Upload: Jan Niezbędny 2012
endmodule
