// Logisim project lololol.circ as structural Verilog: 1 circuit, main circuit main
module main (
  input  in_1,
  output out_2,
  output out_3
);

  wire and_1_out, and_2_out, clock_1_out, d_ff_1_q, d_ff_1_qn, d_ff_2_q, d_ff_2_qn;

  Clock #(.highDuration(1), .lowDuration(1)) clock_1 (.out(clock_1_out));
  and and_1 (and_1_out, d_ff_1_qn, in_1);
  and and_2 (and_2_out, in_1, d_ff_1_q);
  D_Flip_Flop #(.trigger("rising")) d_ff_1 (
    .clk(clock_1_out), .D(and_1_out), .Q(d_ff_1_q), .Qn(d_ff_1_qn), .preset(1'b0), .en(1'b1), .reset(1'b0));
  D_Flip_Flop #(.trigger("rising")) d_ff_2 (
    .clk(clock_1_out), .D(and_2_out), .Q(d_ff_2_q), .Qn(d_ff_2_qn), .preset(1'b0), .en(1'b1), .reset(1'b0));
  and and_3 (out_2, d_ff_1_qn, d_ff_2_q);
  and and_4 (out_3, d_ff_1_q, d_ff_2_qn);
endmodule
